# Fritzing sketch barndoor (saved by Fritzing 0.7.4b)
breadboards: 2

parts:
  U1 = Voltage Regulator - 5V [package="TO220 [THT]"]
  IC1 = L293D [package=THT]
  U2 = atmega328 [package=dip]
  XTAL1 = CRYSTAL - kHz [frequency="16 Mhz"]
  J1 = female pin header, 2 pins [form="♀ (female)"]
  Power_plug1 = Power plug
  J2 = female pin header, 2 pins [form="♀ (female)"]

nets:
  N1: U1.input_voltage, IC1.+Vmotor, Power_plug1.VCC
  GND: U1.GND, IC1.0V, U2.GND#21, Power_plug1.GND
  N2: U1.output_voltage, IC1.Enable_1, IC1.Enable_2, IC1.+V, U2.VCC
  N3: IC1.In_1, U2.D3_(PWM)
  N4: IC1.Out_1_(_Controlled_by_Enable_1_), J2.pin2
  N5: IC1.Out_2_(_Controlled_by_Enable_1_), J2.pin1
  N6: IC1.In_2, U2.D2
  N7: IC1.In_3, U2.D6_(PWM)
  N8: IC1.Out_3_(_Controlled_by_Enable_2_), J1.pin1
  N9: IC1.Out_4_(_Controlled_by_Enable_2_), J1.pin2
  N10: IC1.In_4, U2.D5_(PWM)
  N11: U2.XLAT1, XTAL1.pin_1
  N12: U2.XLAT2, XTAL1.pin_0
